// Logisim project alu.circ as structural Verilog: 1 circuit, main circuit alu
module alu (
  input  [31:0] A,
  input  [31:0] B,
  input  [3:0] ALUSel,
  output [31:0] ALUResult
);

  wire comparator_1_lt;
  wire [4:0] bit_extender_1_out, bit_extender_2_out, bit_extender_7_out;
  wire [31:0] add0, AND0, mul0, mulh0, mulhu0, multiplier_2_out, OR0, SLL0, SLT0, SRA0, SRL0, SUB0, XOR0;
  wire [63:0] bit_extender_3_out, bit_extender_4_out, bit_extender_5_out, bit_extender_6_out;

  Bit_Extender #(.in_width(32), .out_width(5)) bit_extender_1 (.in(B), .out(bit_extender_1_out));
  Bit_Extender #(.in_width(32), .out_width(5)) bit_extender_2 (.in(B), .out(bit_extender_2_out));
  assign bit_extender_3_out = {{32{A[31]}}, A};  // Bit_Extender bit_extender_3
  assign bit_extender_4_out = {{32{B[31]}}, B};  // Bit_Extender bit_extender_4
  assign bit_extender_5_out = {{32{1'b0}}, A};  // Bit_Extender bit_extender_5
  assign bit_extender_6_out = {{32{1'b0}}, B};  // Bit_Extender bit_extender_6
  Bit_Extender #(.in_width(32), .out_width(5)) bit_extender_7 (.in(B), .out(bit_extender_7_out));
  Adder #(.width(32)) adder_1 (.a(A), .b(B), .out(add0));  // open: cin, cout
  Shifter #(.width(32)) shifter_1 (.in(A), .\dist (bit_extender_1_out), .out(SLL0));
  Comparator #(.width(32)) comparator_1 (.a(A), .b(B), .lt(comparator_1_lt));  // open: gt, eq
  assign SLT0 = {{31{1'b0}}, comparator_1_lt};  // Bit_Extender bit_extender_8
  assign XOR0 = A ^ B;  // XOR_Gate xor_1, 32 bits wide
  Shifter #(.shift("lr"), .width(32)) shifter_2 (.in(A), .\dist (bit_extender_2_out), .out(SRL0));
  assign OR0 = A | B;  // OR_Gate or_1, 32 bits wide
  assign AND0 = A & B;  // AND_Gate and_1, 32 bits wide
  Multiplier #(.width(64)) multiplier_1 (
    .a(bit_extender_3_out), .b(bit_extender_4_out), .out({mulh0, mul0}));  // open: cin, cout
  Multiplier #(.width(64)) multiplier_2 (
    .a(bit_extender_5_out), .b(bit_extender_6_out), .out({mulhu0, multiplier_2_out}));  // open: cin, cout
  Subtractor #(.width(32)) subtractor_1 (.a(A), .b(B), .out(SUB0));  // open: bin, bout
  Shifter #(.shift("ar"), .width(32)) shifter_3 (.in(A), .\dist (bit_extender_7_out), .out(SRA0));
  Multiplexer #(.select(4), .width(32)) multiplexer_1 (
    .in0(add0), .in1(SLL0), .in2(SLT0), .in4(XOR0), .in5(SRL0), .in6(OR0), .in7(AND0), .in8(mul0),
    .in9(mulh0), .in11(mulhu0), .in12(SUB0), .in13(SRA0), .in15(B), .out(ALUResult), .sel(ALUSel));  // open: in3, in10, in14

  // Other names for the same wires on the sheet: BSEL0[31:0] = B

  // Notes on the sheet:
  //   INPUTS to your circuit
  //   DON'T CHANGE THE LOCATIONS OF THE INPUTS AND OUTPUTS!
  //   OUTPUT from your circuit
endmodule
