// Logisim project control-logic.circ as structural Verilog: 1 circuit, main circuit control_logic
module control_logic (
  input  [31:0] Instruction,
  input  BrEq,
  input  BrLt,
  output PCSel,
  output RegWEn,
  output [2:0] ImmSel,
  output BrUn,
  output ASel,
  output BSel,
  output [3:0] ALUSel,
  output MemWEn,
  output [1:0] WBSel
);

  wire Add0, Addi0, And0, and_2_out, and_3_out, and_4_out, and_5_out, and_6_out, and_7_out, and_8_out,
       and_9_out, and_10_out, and_11_out, and_12_out, and_13_out, and_29_out, and_32_out, and_33_out,
       and_48_out, and_49_out, and_50_out, and_51_out, and_52_out, and_53_out, Andi0, Auipc0, Beq0, Bge0,
       Bgeu0, Blt0, Bltu0, Bne0, comparator_1_eq, comparator_2_eq, comparator_3_eq, comparator_4_eq,
       comparator_5_eq, comparator_6_eq, comparator_7_eq, comparator_8_eq, comparator_9_eq, comparator_10_eq,
       comparator_11_eq, comparator_12_eq, comparator_13_eq, comparator_14_eq, comparator_15_eq,
       comparator_16_eq, comparator_17_eq, comparator_18_eq, comparator_19_eq, comparator_20_eq,
       comparator_21_eq, comparator_22_eq, comparator_23_eq, comparator_24_eq, comparator_25_eq,
       comparator_26_eq, comparator_27_eq, comparator_28_eq, comparator_29_eq, comparator_30_eq,
       comparator_31_eq, comparator_32_eq, comparator_33_eq, comparator_34_eq, comparator_35_eq,
       comparator_36_eq, comparator_37_eq, comparator_38_eq, comparator_39_eq, comparator_40_eq,
       comparator_41_eq, comparator_42_eq, comparator_43_eq, comparator_44_eq, comparator_45_eq,
       comparator_46_eq, comparator_47_eq, comparator_48_eq, comparator_49_eq, comparator_50_eq,
       comparator_51_eq, comparator_52_eq, comparator_53_eq, comparator_54_eq, comparator_55_eq,
       comparator_56_eq, comparator_57_eq, comparator_58_eq, comparator_59_eq, comparator_60_eq,
       comparator_61_eq, comparator_62_eq, comparator_63_eq, comparator_64_eq, comparator_65_eq,
       comparator_66_eq, comparator_67_eq, comparator_68_eq, comparator_69_eq, comparator_70_eq,
       comparator_71_eq, comparator_72_eq, comparator_73_eq, comparator_74_eq, comparator_75_eq,
       comparator_76_eq, comparator_77_eq, comparator_78_eq, comparator_79_eq, comparator_83_eq,
       comparator_84_eq, Jal0, Jalr0, Lb0, Lh0, Lui0, Lw0, Mul0, Mulh0, Mulhu0, not_1_out, not_2_out,
       not_3_out, Or0, or_1_out, or_2_out, or_3_out, or_4_out, or_5_out, or_6_out, Ori0, Sb0, Sh0, Sll0,
       Slli0, Slt0, Slti0, Sra0, Srai0, Srl0, Srli0, Sub0, Sw0, Xor0, Xori0;
  wire [5:0] RomInput;
  wire [15:14] rom_1_data;

  ROM #(.addrWidth(6), .dataWidth(16)) rom_1 (
    .addr(RomInput), .data({rom_1_data, WBSel, MemWEn, ALUSel, BSel, ASel, BrUn, ImmSel, RegWEn}));
  Comparator #(.width(7)) comparator_1 (.a(7'b0010011), .b(Instruction[6:0]), .eq(comparator_1_eq));  // open: gt, lt
  Comparator #(.width(3)) comparator_2 (.a(Instruction[14:12]), .b(3'b000), .eq(comparator_2_eq));  // open: gt, lt
  Comparator #(.width(7)) comparator_3 (.a(7'b0110011), .b(Instruction[6:0]), .eq(comparator_3_eq));  // open: gt, lt
  Comparator #(.width(3)) comparator_4 (.a(Instruction[14:12]), .b(3'b000), .eq(comparator_4_eq));  // open: gt, lt
  Comparator #(.width(7)) comparator_5 (.a(Instruction[31:25]), .b({7{1'b0}}), .eq(comparator_5_eq));  // open: gt, lt
  Comparator #(.width(7)) comparator_6 (.a(7'b0110011), .b(Instruction[6:0]), .eq(comparator_6_eq));  // open: gt, lt
  Comparator #(.width(3)) comparator_7 (.a(Instruction[14:12]), .b(3'b000), .eq(comparator_7_eq));  // open: gt, lt
  Comparator #(.width(7)) comparator_8 (.a(Instruction[31:25]), .b(7'b0000001), .eq(comparator_8_eq));  // open: gt, lt
  Comparator #(.width(7)) comparator_9 (.a(7'b0110011), .b(Instruction[6:0]), .eq(comparator_9_eq));  // open: gt, lt
  Comparator #(.width(3)) comparator_10 (.a(Instruction[14:12]), .b(3'b000), .eq(comparator_10_eq));  // open: gt, lt
  Comparator #(.width(7)) comparator_11 (
    .a(Instruction[31:25]), .b(7'b0100000), .eq(comparator_11_eq));  // open: gt, lt
  Comparator #(.width(7)) comparator_12 (.a(7'b0110011), .b(Instruction[6:0]), .eq(comparator_12_eq));  // open: gt, lt
  Comparator #(.width(3)) comparator_13 (.a(Instruction[14:12]), .b(3'b001), .eq(comparator_13_eq));  // open: gt, lt
  Comparator #(.width(7)) comparator_14 (.a(Instruction[31:25]), .b({7{1'b0}}), .eq(comparator_14_eq));  // open: gt, lt
  Comparator #(.width(7)) comparator_15 (.a(7'b0110011), .b(Instruction[6:0]), .eq(comparator_15_eq));  // open: gt, lt
  Comparator #(.width(3)) comparator_16 (.a(Instruction[14:12]), .b(3'b001), .eq(comparator_16_eq));  // open: gt, lt
  Comparator #(.width(7)) comparator_17 (
    .a(Instruction[31:25]), .b(7'b0000001), .eq(comparator_17_eq));  // open: gt, lt
  Comparator #(.width(7)) comparator_18 (.a(7'b0110011), .b(Instruction[6:0]), .eq(comparator_18_eq));  // open: gt, lt
  Comparator #(.width(3)) comparator_19 (.a(Instruction[14:12]), .b(3'b011), .eq(comparator_19_eq));  // open: gt, lt
  Comparator #(.width(7)) comparator_20 (
    .a(Instruction[31:25]), .b(7'b0000001), .eq(comparator_20_eq));  // open: gt, lt
  Comparator #(.width(7)) comparator_21 (.a(7'b0110011), .b(Instruction[6:0]), .eq(comparator_21_eq));  // open: gt, lt
  Comparator #(.width(3)) comparator_22 (.a(Instruction[14:12]), .b(3'b010), .eq(comparator_22_eq));  // open: gt, lt
  Comparator #(.width(7)) comparator_23 (.a(Instruction[31:25]), .b({7{1'b0}}), .eq(comparator_23_eq));  // open: gt, lt
  Comparator #(.width(7)) comparator_24 (.a(7'b0110011), .b(Instruction[6:0]), .eq(comparator_24_eq));  // open: gt, lt
  Comparator #(.width(3)) comparator_25 (.a(Instruction[14:12]), .b(3'b100), .eq(comparator_25_eq));  // open: gt, lt
  Comparator #(.width(7)) comparator_26 (.a(Instruction[31:25]), .b({7{1'b0}}), .eq(comparator_26_eq));  // open: gt, lt
  Comparator #(.width(7)) comparator_27 (.a(7'b0110011), .b(Instruction[6:0]), .eq(comparator_27_eq));  // open: gt, lt
  Comparator #(.width(3)) comparator_28 (.a(Instruction[14:12]), .b(3'b101), .eq(comparator_28_eq));  // open: gt, lt
  Comparator #(.width(7)) comparator_29 (.a(Instruction[31:25]), .b({7{1'b0}}), .eq(comparator_29_eq));  // open: gt, lt
  Comparator #(.width(7)) comparator_30 (.a(7'b0110011), .b(Instruction[6:0]), .eq(comparator_30_eq));  // open: gt, lt
  Comparator #(.width(3)) comparator_31 (.a(Instruction[14:12]), .b(3'b101), .eq(comparator_31_eq));  // open: gt, lt
  Comparator #(.width(7)) comparator_32 (
    .a(Instruction[31:25]), .b(7'b0100000), .eq(comparator_32_eq));  // open: gt, lt
  Comparator #(.width(7)) comparator_33 (.a(7'b0110011), .b(Instruction[6:0]), .eq(comparator_33_eq));  // open: gt, lt
  Comparator #(.width(3)) comparator_34 (.a(Instruction[14:12]), .b(3'b110), .eq(comparator_34_eq));  // open: gt, lt
  Comparator #(.width(7)) comparator_35 (.a(Instruction[31:25]), .b({7{1'b0}}), .eq(comparator_35_eq));  // open: gt, lt
  Comparator #(.width(7)) comparator_36 (.a(7'b0110011), .b(Instruction[6:0]), .eq(comparator_36_eq));  // open: gt, lt
  Comparator #(.width(3)) comparator_37 (.a(Instruction[14:12]), .b(3'b110), .eq(comparator_37_eq));  // open: gt, lt
  Comparator #(.width(7)) comparator_38 (.a(Instruction[31:25]), .b({7{1'b0}}), .eq(comparator_38_eq));  // open: gt, lt
  and and_1 (Addi0, comparator_1_eq, comparator_2_eq);
  and and_2 (and_2_out, comparator_3_eq, comparator_4_eq);
  and and_3 (and_3_out, comparator_6_eq, comparator_7_eq);
  and and_4 (and_4_out, comparator_9_eq, comparator_10_eq);
  and and_5 (and_5_out, comparator_12_eq, comparator_13_eq);
  and and_6 (and_6_out, comparator_15_eq, comparator_16_eq);
  and and_7 (and_7_out, comparator_18_eq, comparator_19_eq);
  and and_8 (and_8_out, comparator_21_eq, comparator_22_eq);
  and and_9 (and_9_out, comparator_24_eq, comparator_25_eq);
  and and_10 (and_10_out, comparator_27_eq, comparator_28_eq);
  and and_11 (and_11_out, comparator_30_eq, comparator_31_eq);
  and and_12 (and_12_out, comparator_33_eq, comparator_34_eq);
  and and_13 (and_13_out, comparator_36_eq, comparator_37_eq);
  and and_14 (Add0, and_2_out, comparator_5_eq);
  and and_15 (Mul0, and_3_out, comparator_8_eq);
  and and_16 (Sub0, and_4_out, comparator_11_eq);
  and and_17 (Sll0, and_5_out, comparator_14_eq);
  and and_18 (Mulh0, and_6_out, comparator_17_eq);
  and and_19 (Mulhu0, and_7_out, comparator_20_eq);
  and and_20 (Slt0, and_8_out, comparator_23_eq);
  and and_21 (Xor0, and_9_out, comparator_26_eq);
  and and_22 (Srl0, and_10_out, comparator_29_eq);
  and and_23 (Sra0, and_11_out, comparator_32_eq);
  and and_24 (Or0, and_12_out, comparator_35_eq);
  and and_25 (And0, and_13_out, comparator_38_eq);
  Comparator #(.width(7)) comparator_39 (.a(7'b0000011), .b(Instruction[6:0]), .eq(comparator_39_eq));  // open: gt, lt
  Comparator #(.width(3)) comparator_40 (.a(Instruction[14:12]), .b(3'b000), .eq(comparator_40_eq));  // open: gt, lt
  Comparator #(.width(7)) comparator_41 (.a(7'b0000011), .b(Instruction[6:0]), .eq(comparator_41_eq));  // open: gt, lt
  Comparator #(.width(3)) comparator_42 (.a(Instruction[14:12]), .b(3'b001), .eq(comparator_42_eq));  // open: gt, lt
  Comparator #(.width(7)) comparator_43 (.a(7'b0000011), .b(Instruction[6:0]), .eq(comparator_43_eq));  // open: gt, lt
  Comparator #(.width(3)) comparator_44 (.a(Instruction[14:12]), .b(3'b010), .eq(comparator_44_eq));  // open: gt, lt
  Comparator #(.width(7)) comparator_45 (.a(7'b0010011), .b(Instruction[6:0]), .eq(comparator_45_eq));  // open: gt, lt
  Comparator #(.width(3)) comparator_46 (.a(Instruction[14:12]), .b(3'b001), .eq(comparator_46_eq));  // open: gt, lt
  Comparator #(.width(7)) comparator_47 (.a(Instruction[31:25]), .b({7{1'b0}}), .eq(comparator_47_eq));  // open: gt, lt
  Comparator #(.width(7)) comparator_48 (.a(7'b0010011), .b(Instruction[6:0]), .eq(comparator_48_eq));  // open: gt, lt
  Comparator #(.width(3)) comparator_49 (.a(Instruction[14:12]), .b(3'b010), .eq(comparator_49_eq));  // open: gt, lt
  Comparator #(.width(7)) comparator_50 (.a(7'b0010011), .b(Instruction[6:0]), .eq(comparator_50_eq));  // open: gt, lt
  Comparator #(.width(3)) comparator_51 (.a(Instruction[14:12]), .b(3'b100), .eq(comparator_51_eq));  // open: gt, lt
  Comparator #(.width(7)) comparator_52 (.a(7'b0010011), .b(Instruction[6:0]), .eq(comparator_52_eq));  // open: gt, lt
  Comparator #(.width(3)) comparator_53 (.a(Instruction[14:12]), .b(3'b101), .eq(comparator_53_eq));  // open: gt, lt
  Comparator #(.width(7)) comparator_54 (.a(Instruction[31:25]), .b({7{1'b0}}), .eq(comparator_54_eq));  // open: gt, lt
  Comparator #(.width(7)) comparator_55 (.a(7'b0010011), .b(Instruction[6:0]), .eq(comparator_55_eq));  // open: gt, lt
  Comparator #(.width(3)) comparator_56 (.a(Instruction[14:12]), .b(3'b101), .eq(comparator_56_eq));  // open: gt, lt
  Comparator #(.width(7)) comparator_57 (
    .a(Instruction[31:25]), .b(7'b0100000), .eq(comparator_57_eq));  // open: gt, lt
  Comparator #(.width(7)) comparator_58 (.a(7'b0010011), .b(Instruction[6:0]), .eq(comparator_58_eq));  // open: gt, lt
  Comparator #(.width(3)) comparator_59 (.a(Instruction[14:12]), .b(3'b110), .eq(comparator_59_eq));  // open: gt, lt
  Comparator #(.width(7)) comparator_60 (.a(7'b0010011), .b(Instruction[6:0]), .eq(comparator_60_eq));  // open: gt, lt
  Comparator #(.width(3)) comparator_61 (.a(Instruction[14:12]), .b(3'b111), .eq(comparator_61_eq));  // open: gt, lt
  Comparator #(.width(7)) comparator_62 (.a(7'b0100011), .b(Instruction[6:0]), .eq(comparator_62_eq));  // open: gt, lt
  Comparator #(.width(3)) comparator_63 (.a(Instruction[14:12]), .b(3'b000), .eq(comparator_63_eq));  // open: gt, lt
  Comparator #(.width(7)) comparator_64 (.a(7'b0100011), .b(Instruction[6:0]), .eq(comparator_64_eq));  // open: gt, lt
  Comparator #(.width(3)) comparator_65 (.a(Instruction[14:12]), .b(3'b001), .eq(comparator_65_eq));  // open: gt, lt
  Comparator #(.width(7)) comparator_66 (.a(7'b0100011), .b(Instruction[6:0]), .eq(comparator_66_eq));  // open: gt, lt
  Comparator #(.width(3)) comparator_67 (.a(Instruction[14:12]), .b(3'b010), .eq(comparator_67_eq));  // open: gt, lt
  Comparator #(.width(7)) comparator_68 (.a(7'b1100011), .b(Instruction[6:0]), .eq(comparator_68_eq));  // open: gt, lt
  Comparator #(.width(3)) comparator_69 (.a(Instruction[14:12]), .b(3'b000), .eq(comparator_69_eq));  // open: gt, lt
  Comparator #(.width(7)) comparator_70 (.a(7'b1100011), .b(Instruction[6:0]), .eq(comparator_70_eq));  // open: gt, lt
  Comparator #(.width(3)) comparator_71 (.a(Instruction[14:12]), .b(3'b001), .eq(comparator_71_eq));  // open: gt, lt
  Comparator #(.width(7)) comparator_72 (.a(7'b1100011), .b(Instruction[6:0]), .eq(comparator_72_eq));  // open: gt, lt
  Comparator #(.width(3)) comparator_73 (.a(Instruction[14:12]), .b(3'b100), .eq(comparator_73_eq));  // open: gt, lt
  Comparator #(.width(7)) comparator_74 (.a(7'b1100011), .b(Instruction[6:0]), .eq(comparator_74_eq));  // open: gt, lt
  Comparator #(.width(3)) comparator_75 (.a(Instruction[14:12]), .b(3'b101), .eq(comparator_75_eq));  // open: gt, lt
  Comparator #(.width(7)) comparator_76 (.a(7'b1100011), .b(Instruction[6:0]), .eq(comparator_76_eq));  // open: gt, lt
  Comparator #(.width(3)) comparator_77 (.a(Instruction[14:12]), .b(3'b110), .eq(comparator_77_eq));  // open: gt, lt
  Comparator #(.width(7)) comparator_78 (.a(7'b1100011), .b(Instruction[6:0]), .eq(comparator_78_eq));  // open: gt, lt
  Comparator #(.width(3)) comparator_79 (.a(Instruction[14:12]), .b(3'b111), .eq(comparator_79_eq));  // open: gt, lt
  and and_26 (Lb0, comparator_39_eq, comparator_40_eq);
  and and_27 (Lh0, comparator_41_eq, comparator_42_eq);
  and and_28 (Lw0, comparator_43_eq, comparator_44_eq);
  and and_29 (and_29_out, comparator_45_eq, comparator_46_eq);
  and and_30 (Slti0, comparator_48_eq, comparator_49_eq);
  and and_31 (Xori0, comparator_50_eq, comparator_51_eq);
  and and_32 (and_32_out, comparator_52_eq, comparator_53_eq);
  and and_33 (and_33_out, comparator_55_eq, comparator_56_eq);
  and and_34 (Ori0, comparator_58_eq, comparator_59_eq);
  and and_35 (Andi0, comparator_60_eq, comparator_61_eq);
  and and_36 (Sb0, comparator_62_eq, comparator_63_eq);
  and and_37 (Sh0, comparator_64_eq, comparator_65_eq);
  and and_38 (Sw0, comparator_66_eq, comparator_67_eq);
  and and_39 (Beq0, comparator_68_eq, comparator_69_eq);
  and and_40 (Bne0, comparator_70_eq, comparator_71_eq);
  and and_41 (Blt0, comparator_72_eq, comparator_73_eq);
  and and_42 (Bge0, comparator_74_eq, comparator_75_eq);
  and and_43 (Bltu0, comparator_76_eq, comparator_77_eq);
  and and_44 (Bgeu0, comparator_78_eq, comparator_79_eq);
  and and_45 (Slli0, and_29_out, comparator_47_eq);
  and and_46 (Srli0, and_32_out, comparator_54_eq);
  and and_47 (Srai0, and_33_out, comparator_57_eq);
  not not_1 (not_1_out, BrEq);
  not not_2 (not_2_out, BrLt);
  not not_3 (not_3_out, BrLt);
  Comparator #(.width(7)) comparator_80 (.a(Instruction[6:0]), .b(7'b0010111), .eq(Auipc0));  // open: gt, lt
  Comparator #(.width(7)) comparator_81 (.a(Instruction[6:0]), .b(7'b0110111), .eq(Lui0));  // open: gt, lt
  Comparator #(.width(7)) comparator_82 (.a(Instruction[6:0]), .b(7'b1101111), .eq(Jal0));  // open: gt, lt
  Comparator #(.width(7)) comparator_83 (.a(7'b1100111), .b(Instruction[6:0]), .eq(comparator_83_eq));  // open: gt, lt
  Comparator #(.width(3)) comparator_84 (.a(Instruction[14:12]), .b(3'b000), .eq(comparator_84_eq));  // open: gt, lt
  and and_48 (and_48_out, Beq0, BrEq);
  and and_49 (and_49_out, Bne0, not_1_out);
  and and_50 (and_50_out, Bge0, not_2_out);
  and and_51 (and_51_out, Bgeu0, not_3_out);
  and and_52 (and_52_out, Blt0, BrLt);
  and and_53 (and_53_out, Bltu0, BrLt);
  and and_54 (Jalr0, comparator_83_eq, comparator_84_eq);
  or or_1 (or_1_out, and_48_out, and_49_out);
  or or_2 (or_2_out, and_50_out, and_51_out);
  or or_3 (or_3_out, and_52_out, and_53_out);
  or or_4 (or_4_out, or_1_out, or_2_out);
  or or_5 (or_5_out, or_4_out, or_3_out);
  or or_6 (or_6_out, or_5_out, Jal0);
  or or_7 (PCSel, or_6_out, Jalr0);
  Priority_Encoder #(.select_enc(6)) priority_encoder_1 (
    .in0(Add0), .in1(Mul0), .in2(Sub0), .in3(Sll0), .in4(Mulh0), .in5(Mulhu0), .in6(Slt0), .in7(Xor0),
    .in8(Srl0), .in9(Sra0), .in10(Or0), .in11(And0), .in12(Lb0), .in13(Lh0), .in14(Lw0), .in15(Addi0),
    .in16(Slli0), .in17(Slti0), .in18(Xori0), .in19(Srli0), .in20(Srai0), .in21(Ori0), .in22(Andi0),
    .in23(Sb0), .in24(Sh0), .in25(Sw0), .in26(Beq0), .in27(Bne0), .in28(Blt0), .in29(Bge0), .in30(Bltu0),
    .in31(Bgeu0), .in32(Auipc0), .in33(Lui0), .in34(Jal0), .in35(Jalr0), .out(RomInput));  // open: in36, in37, in38, in39, in40, in41, in42, in43, in44, in45, in46, in47, in48, in49, in50, in51, in52, in53, in54, in55, in56, in57, in58, in59, in60, in61, in62, in63, gs, en_out, en_in

  // Notes on the sheet:
  //   INPUTS to your circuit
  //   contents of rom_1 (hex, n*v repeats v):
  //   1 401 601 81 481 581 101 201 281 681 301 381 1041 1041 1041 41 c1 141 241 2c1 6c1 341 3c1 842 842
  //   842 4*64 74 74 67 7c7 2069 2041 4*0 1 401 601 81 481 581 101 201 281 681 301 381 1041 1041 1041 41
  //   c3 141 241 2c3 6c3 341 3c1 844
  //   ROM FOR CONTROL LOGIC
  //   DON'T CHANGE THE LOCATIONS OF THE INPUTS AND OUTPUTS!
  //   This is only if you choose to do the ROM option
  //   OUTPUT from your circuit
  //   Reminder: If using ROM, use combinational logic for PCSel
endmodule
