// Logisim project partial-store.circ as structural Verilog: 1 circuit, main circuit partial_store
module partial_store (
  input  [31:0] Instruction,
  input  [31:0] MemAddress,
  input  [31:0] DataFromReg,
  input  MemRW,
  output [3:0] MemWriteMask,
  output [31:0] DataToMem
);

  wire comparator_1_eq, comparator_2_eq, comparator_3_eq, comparator_4_eq, comparator_5_eq, comparator_6_eq,
       NonStore0, or_1_out, or_2_out, Sb0, Sh0, Sw0;
  wire [1:0] MemAddressLast2, SSel;
  wire [3:0] SbMemMask0, ShMemMask0;
  wire [7:0] DataFromRegLast8;
  wire [15:0] DataFromRegLast16;
  wire [31:0] bit_extender_4_out, bit_extender_5_out, SbDataToMem0, ShDataToMem0;

  or or_1 (or_1_out, Sb0, Sh0);
  or or_2 (or_2_out, or_1_out, Sw0);
  Bit_Extender #(.in_width(32), .out_width(2)) bit_extender_1 (.in(MemAddress), .out(MemAddressLast2));
  Comparator #(.width(7)) comparator_1 (.a(7'b0100011), .b(Instruction[6:0]), .eq(comparator_1_eq));  // open: gt, lt
  Comparator #(.width(3)) comparator_2 (.a(Instruction[14:12]), .b(3'b000), .eq(comparator_2_eq));  // open: gt, lt
  Comparator #(.width(7)) comparator_3 (.a(7'b0100011), .b(Instruction[6:0]), .eq(comparator_3_eq));  // open: gt, lt
  Comparator #(.width(3)) comparator_4 (.a(Instruction[14:12]), .b(3'b001), .eq(comparator_4_eq));  // open: gt, lt
  Comparator #(.width(7)) comparator_5 (.a(7'b0100011), .b(Instruction[6:0]), .eq(comparator_5_eq));  // open: gt, lt
  Comparator #(.width(3)) comparator_6 (.a(Instruction[14:12]), .b(3'b010), .eq(comparator_6_eq));  // open: gt, lt
  not not_1 (NonStore0, or_2_out);
  Priority_Encoder #(.select_enc(2)) priority_encoder_1 (
    .in0(Sb0), .in1(Sh0), .in2(Sw0), .in3(NonStore0), .out(SSel));  // open: gs, en_out, en_in
  and and_1 (Sb0, comparator_1_eq, comparator_2_eq);
  and and_2 (Sh0, comparator_3_eq, comparator_4_eq);
  and and_3 (Sw0, comparator_5_eq, comparator_6_eq);
  Multiplexer #(.select(2), .width(32)) multiplexer_1 (
    .in0(SbDataToMem0), .in1(ShDataToMem0), .in2(DataFromReg), .in3({32{1'b0}}), .out(DataToMem), .sel(SSel));
  Multiplexer #(.select(2), .width(4)) multiplexer_2 (
    .in0(SbMemMask0), .in1(ShMemMask0), .in2(4'b1111), .in3(4'b0000), .out(MemWriteMask), .sel(SSel));
  Bit_Extender #(.in_width(32), .out_width(8)) bit_extender_2 (.in(DataFromReg), .out(DataFromRegLast8));
  Bit_Extender #(.in_width(32)) bit_extender_3 (.in(DataFromReg), .out(DataFromRegLast16));
  assign bit_extender_4_out = {{24{1'b0}}, DataFromRegLast8};  // Bit_Extender bit_extender_4
  Multiplexer #(.select(2), .width(4)) multiplexer_3 (
    .in0(4'b0001), .in1(4'b0010), .in2(4'b0100), .in3(4'b1000), .out(SbMemMask0), .sel(MemAddressLast2));
  Multiplexer #(.select(2), .width(32)) multiplexer_4 (
    .in0(bit_extender_4_out), .in1({{16{1'b0}}, DataFromRegLast8, {8{1'b0}}}),
    .in2({{8{1'b0}}, DataFromRegLast8, {16{1'b0}}}), .in3({DataFromRegLast8, {24{1'b0}}}),
    .out(SbDataToMem0), .sel(MemAddressLast2));
  assign bit_extender_5_out = {{16{1'b0}}, DataFromRegLast16};  // Bit_Extender bit_extender_5
  Multiplexer #(.width(4)) multiplexer_5 (.in0(4'b0011), .in1(4'b1100), .out(ShMemMask0), .sel(MemAddress[1]));
  Multiplexer #(.width(32)) multiplexer_6 (
    .in0(bit_extender_5_out), .in1({DataFromRegLast16, {16{1'b0}}}), .out(ShDataToMem0), .sel(MemAddress[1]));

  // Other names for the same wires on the sheet: MemAddressLast2nd = MemAddress[1]; SwDataToMem0[31:0] = DataFromReg

  // Notes on the sheet:
  //   INPUTS to your circuit
  //   DON'T CHANGE THE LOCATIONS OF THE INPUTS AND OUTPUTS!
  //   OUTPUT from your circuit
endmodule
